# Fritzing sketch ESP8266_Alexa_IR_controller_w_transistor_2 (saved by Fritzing 0.9.9b)
breadboards: 1

parts:
  U1 = NodeMCU V1.0
  2N2222A_NPN = TRANSISTOR_NPN [package=to-92-ammo]
  R1 = Resistor [tolerance=±5% power=0.25 resistance=470 package=THT]
  IR_LED = Infrared LED - 5mm [package="5 mm [THT]"]
  R2 = Resistor [tolerance=±5% power=0.25 resistance=220 package=THT]

nets:
  N1: U1.D1, R2.Pin_1
  N2: U1.3V3, R1.Pin_1
  N3: U1.GND, 2N2222A_NPN.E
  N4: 2N2222A_NPN.B, R2.Pin_0
  N5: 2N2222A_NPN.C, IR_LED.cathode
  N6: R1.Pin_0, IR_LED.anode

custom parts:
  NodeMCU V1.0: ESP8266 based NodeMCU
  Infrared LED - 5mm: A generic infrared LED (~1.2V)
